# Fritzing sketch IR Reciever Controller (saved by Fritzing 0.9.3b)
breadboards: 1

parts:
  Part1 = Arduino Uno (Rev3)
  IR1 = TSOP312.., 314.. [package=THT]
  LED1 = LED - 5mm [color="Red (633nm)" package="5 mm [THT]"]
  LED2 = LED - 5mm [color="Red (633nm)" package="5 mm [THT]"]
  LED3 = LED - 5mm [color="Red (633nm)" package="5 mm [THT]"]
  R1 = Resistor [tolerance=±5% resistance=220 package=THT]
  R2 = Resistor [tolerance=±5% resistance=220 package=THT]
  R3 = Resistor [tolerance=±5% resistance=220 package=THT]

nets:
  N1: Part1.D13/SCK, IR1.GND
  N2: Part1.D2, LED3.anode
  N3: Part1.D3_PWM, LED2.anode
  N4: Part1.D4, LED1.anode
  N5: Part1.5V, IR1.Data
  N6: Part1.GND, IR1.Vs, R1.Pin_0, R2.Pin_0, R3.Pin_0
  N7: LED1.cathode, R3.Pin_1
  N8: LED2.cathode, R2.Pin_1
  N9: LED3.cathode, R1.Pin_1
